# Fritzing sketch EnergyMeter (saved by Fritzing 0.9.2b)
breadboards: 1

parts:
  R1 = Resistor [tolerance=±5% resistance=33 package="0603 [SMD]"]
  Part1 = TRRS 3.5mm Jack Breakout
  R2 = Resistor [tolerance=±5% resistance=10k package="0603 [SMD]"]
  R3 = Resistor [tolerance=±5% resistance=10k package="0603 [SMD]"]
  C1 = Electrolytic Capacitor [capacitance=10µF voltage=20V package="100 mil [THT, electrolytic]"]
  TRINKET1 = Trinket 5V

nets:
  N1: R1.Pin_0, Part1.TIP, TRINKET1.no_name_yet#7
  N2: R1.Pin_1, Part1.SLEEVE, R2.Pin_1, R3.Pin_1, C1.-
  N3: R2.Pin_0, TRINKET1.no_name_yet#6
  N4: R3.Pin_0, C1.+, TRINKET1.no_name_yet#2

custom parts:
  Trinket 5V: Adafruit Trinket 5V
