# Fritzing sketch EnergyMeter_Mini (saved by Fritzing 0.9.2b)
circuit board: 8.46667cm x 5.64444cm
breadboards: 1

parts:
  TRINKET1 = Trinket 5V
  C1 = Electrolytic Capacitor [capacitance=10μF voltage=20V package="0605 [SMD, electrolytic]"]
  R2 = Resistor [tolerance=±5% resistance=10k package="2010 [SMD]"]
  R3 = Resistor [tolerance=±5% resistance=10k package="2010 [SMD]"]
  R1 = Resistor [tolerance=±5% resistance=33 package="2010 [SMD]"]
  CT = TRRS 3.5mm Jack Breakout

nets:
  N1: TRINKET1.no_name_yet#2, C1.-, R2.Pin_1
  N2: TRINKET1.no_name_yet#6, R3.Pin_0
  N3: TRINKET1.no_name_yet#7, R1.Pin_0, CT.TIP
  N4: C1.+, R2.Pin_0, R3.Pin_1, R1.Pin_1, CT.SLEEVE

custom parts:
  Trinket 5V: Adafruit Trinket 5V
